// Logisim project memory_game.circ as structural Verilog
module main (
  input  in_1
);

  wire button_1_out;
  wire [4:0] single_display_1_out_2, single_display_1_out_3, single_display_1_out_4, single_display_1_out_5,
       single_display_1_out_6, single_display_2_out_2, single_display_2_out_3, single_display_2_out_4,
       single_display_2_out_5, single_display_2_out_6, single_display_3_out_2, single_display_3_out_3,
       single_display_3_out_4, single_display_3_out_5, single_display_3_out_6, single_display_4_out_2,
       single_display_4_out_3, single_display_4_out_4, single_display_4_out_5, single_display_4_out_6,
       single_display_5_out_2, single_display_5_out_3, single_display_5_out_4, single_display_5_out_5,
       single_display_5_out_6, single_display_mirrored_1_out_2, single_display_mirrored_1_out_3,
       single_display_mirrored_1_out_4, single_display_mirrored_1_out_5, single_display_mirrored_1_out_6,
       single_display_mirrored_2_out_2, single_display_mirrored_2_out_3, single_display_mirrored_2_out_4,
       single_display_mirrored_2_out_5, single_display_mirrored_2_out_6, single_display_mirrored_3_out_2,
       single_display_mirrored_3_out_3, single_display_mirrored_3_out_4, single_display_mirrored_3_out_5,
       single_display_mirrored_3_out_6, single_display_mirrored_4_out_2, single_display_mirrored_4_out_3,
       single_display_mirrored_4_out_4, single_display_mirrored_4_out_5, single_display_mirrored_4_out_6,
       single_display_mirrored_5_out_2, single_display_mirrored_5_out_3, single_display_mirrored_5_out_4,
       single_display_mirrored_5_out_5, single_display_mirrored_5_out_6;
  wire [8:0] d0, d1, d2, d3, d4, d5, d6, d7, d8, d9;

  Button button_1 (.out(button_1_out));
  Hex_Digit_Display hex_digit_display_1 ();  // open: value, dp
  Hex_Digit_Display hex_digit_display_2 ();  // open: value, dp
  single_display single_display_1 (
    .in_1(d0), .out_2(single_display_1_out_2), .out_3(single_display_1_out_3),
    .out_4(single_display_1_out_4), .out_5(single_display_1_out_5), .out_6(single_display_1_out_6));
  DotMatrix #(.matrixrows(5)) dotmatrix_1 (
    .col0(single_display_1_out_6), .col1(single_display_1_out_5), .col2(single_display_1_out_4),
    .col3(single_display_1_out_3), .col4(single_display_1_out_2));
  DotMatrix #(.matrixrows(5)) dotmatrix_2 (
    .col0(single_display_2_out_6), .col1(single_display_2_out_5), .col2(single_display_2_out_4),
    .col3(single_display_2_out_3), .col4(single_display_2_out_2));
  DotMatrix #(.matrixrows(5)) dotmatrix_3 (
    .col0(single_display_mirrored_1_out_2), .col1(single_display_mirrored_1_out_3),
    .col2(single_display_mirrored_1_out_4), .col3(single_display_mirrored_1_out_5),
    .col4(single_display_mirrored_1_out_6));
  DotMatrix #(.matrixrows(5)) dotmatrix_4 (
    .col0(single_display_mirrored_2_out_2), .col1(single_display_mirrored_2_out_3),
    .col2(single_display_mirrored_2_out_4), .col3(single_display_mirrored_2_out_5),
    .col4(single_display_mirrored_2_out_6));
  single_display_mirrored single_display_mirrored_1 (
    .in_1(d1), .out_2(single_display_mirrored_1_out_2), .out_3(single_display_mirrored_1_out_3),
    .out_4(single_display_mirrored_1_out_4), .out_5(single_display_mirrored_1_out_5),
    .out_6(single_display_mirrored_1_out_6));
  single_display_mirrored single_display_mirrored_2 (
    .in_1(d3), .out_2(single_display_mirrored_2_out_2), .out_3(single_display_mirrored_2_out_3),
    .out_4(single_display_mirrored_2_out_4), .out_5(single_display_mirrored_2_out_5),
    .out_6(single_display_mirrored_2_out_6));
  Button button_2 ();  // open: out
  Button button_3 ();  // open: out
  single_display single_display_2 (
    .in_1(d2), .out_2(single_display_2_out_2), .out_3(single_display_2_out_3),
    .out_4(single_display_2_out_4), .out_5(single_display_2_out_5), .out_6(single_display_2_out_6));
  DotMatrix #(.matrixrows(5)) dotmatrix_5 (
    .col0(single_display_3_out_6), .col1(single_display_3_out_5), .col2(single_display_3_out_4),
    .col3(single_display_3_out_3), .col4(single_display_3_out_2));
  DotMatrix #(.matrixrows(5)) dotmatrix_6 (
    .col0(single_display_mirrored_3_out_2), .col1(single_display_mirrored_3_out_3),
    .col2(single_display_mirrored_3_out_4), .col3(single_display_mirrored_3_out_5),
    .col4(single_display_mirrored_3_out_6));
  single_display_mirrored single_display_mirrored_3 (
    .in_1(d5), .out_2(single_display_mirrored_3_out_2), .out_3(single_display_mirrored_3_out_3),
    .out_4(single_display_mirrored_3_out_4), .out_5(single_display_mirrored_3_out_5),
    .out_6(single_display_mirrored_3_out_6));
  Button button_4 ();  // open: out
  Button button_5 ();  // open: out
  Button button_6 ();  // open: out
  Button button_7 ();  // open: out
  Hex_Digit_Display hex_digit_display_3 ();  // open: value, dp
  single_display single_display_3 (
    .in_1(d4), .out_2(single_display_3_out_2), .out_3(single_display_3_out_3),
    .out_4(single_display_3_out_4), .out_5(single_display_3_out_5), .out_6(single_display_3_out_6));
  single_display single_display_4 (
    .in_1(d6), .out_2(single_display_4_out_2), .out_3(single_display_4_out_3),
    .out_4(single_display_4_out_4), .out_5(single_display_4_out_5), .out_6(single_display_4_out_6));
  DotMatrix #(.matrixrows(5)) dotmatrix_7 (
    .col0(single_display_4_out_6), .col1(single_display_4_out_5), .col2(single_display_4_out_4),
    .col3(single_display_4_out_3), .col4(single_display_4_out_2));
  DotMatrix #(.matrixrows(5)) dotmatrix_8 (
    .col0(single_display_mirrored_4_out_2), .col1(single_display_mirrored_4_out_3),
    .col2(single_display_mirrored_4_out_4), .col3(single_display_mirrored_4_out_5),
    .col4(single_display_mirrored_4_out_6));
  single_display_mirrored single_display_mirrored_4 (
    .in_1(d7), .out_2(single_display_mirrored_4_out_2), .out_3(single_display_mirrored_4_out_3),
    .out_4(single_display_mirrored_4_out_4), .out_5(single_display_mirrored_4_out_5),
    .out_6(single_display_mirrored_4_out_6));
  Button button_8 ();  // open: out
  Button button_9 ();  // open: out
  Button button_10 ();  // open: out
  Button button_11 ();  // open: out
  Hex_Digit_Display hex_digit_display_4 ();  // open: value, dp
  single_display single_display_5 (
    .in_1(d8), .out_2(single_display_5_out_2), .out_3(single_display_5_out_3),
    .out_4(single_display_5_out_4), .out_5(single_display_5_out_5), .out_6(single_display_5_out_6));
  DotMatrix #(.matrixrows(5)) dotmatrix_9 (
    .col0(single_display_5_out_6), .col1(single_display_5_out_5), .col2(single_display_5_out_4),
    .col3(single_display_5_out_3), .col4(single_display_5_out_2));
  DotMatrix #(.matrixrows(5)) dotmatrix_10 (
    .col0(single_display_mirrored_5_out_2), .col1(single_display_mirrored_5_out_3),
    .col2(single_display_mirrored_5_out_4), .col3(single_display_mirrored_5_out_5),
    .col4(single_display_mirrored_5_out_6));
  single_display_mirrored single_display_mirrored_5 (
    .in_1(d9), .out_2(single_display_mirrored_5_out_2), .out_3(single_display_mirrored_5_out_3),
    .out_4(single_display_mirrored_5_out_4), .out_5(single_display_mirrored_5_out_5),
    .out_6(single_display_mirrored_5_out_6));
  \logic  logic_1 (
    .in_1(in_1), .out_2(d0), .out_3(d1), .out_4(d2), .out_5(d3), .out_6(d4), .out_7(d5), .out_8(d6),
    .out_9(d7), .out_10(d8), .out_11(d9));
endmodule

module buttons (
  input  in_1,
  input  in_2,
  input  in_3,
  input  in_4,
  input  in_5,
  input  in_6,
  input  in_7,
  input  in_8,
  input  in_9,
  input  in_10
);
endmodule

module \logic  (
  input  in_1,
  output [8:0] out_2,
  output [8:0] out_3,
  output [8:0] out_4,
  output [8:0] out_5,
  output [8:0] out_6,
  output [8:0] out_7,
  output [8:0] out_8,
  output [8:0] out_9,
  output [8:0] out_10,
  output [8:0] out_11
);

  wire clk;
  wire [3:0] randN;

  deck deck_1 (.set(in_1), .out_2(out_2), .out_3(out_4), .out_4(out_6), .out_5(out_8), .out_6(out_10));
  Clock clock_1 (.out(clk));
  Random #(.width(4)) random_1 (.clk(clk), .out(randN));  // open: clr, next
  buttons buttons_1 ();  // open: in_1, in_2, in_3, in_4, in_5, in_6, in_7, in_8, in_9, in_10
  Register #(.width(3)) register_1 ();  // open: D, en, clk, Q, clr
  Register #(.width(3)) register_2 ();  // open: D, en, clk, Q, clr
  Register #(.width(3)) register_3 ();  // open: D, en, clk, Q, clr
  Register #(.width(3)) register_4 ();  // open: D, en, clk, Q, clr
  Register #(.width(3)) register_5 ();  // open: D, en, clk, Q, clr
  Register #(.width(3)) register_6 ();  // open: D, en, clk, Q, clr
  Register #(.width(3)) register_7 ();  // open: D, en, clk, Q, clr
  Register #(.width(3)) register_8 ();  // open: D, en, clk, Q, clr
  Register #(.width(3)) register_9 ();  // open: D, en, clk, Q, clr
  Register #(.width(3)) register_10 ();  // open: D, en, clk, Q, clr

  assign out_3 = out_2;
  assign out_5 = out_4;
  assign out_7 = out_6;
  assign out_9 = out_8;
  assign out_11 = out_10;

  // Other names for the same wires on the sheet: c0[8:0] = out_2; c1[8:0] = out_4; c2[8:0] = out_6; c3[8:0] = out_8;
  //   c4[8:0] = out_10
endmodule

module deck (
  input  set,
  output [8:0] out_2,
  output [8:0] out_3,
  output [8:0] out_4,
  output [8:0] out_5,
  output [8:0] out_6
);

  wire and_1_out, clock_1_out, clock_2_out, clock_3_out, counter_1_carry, decoder_1_out1, decoder_1_out2,
       decoder_1_out3, decoder_1_out4, decoder_1_out5, not_1_out, not_2_out;
  wire [2:0] counter_1_q;
  wire [8:0] demultiplexer_1_out1, demultiplexer_1_out2, demultiplexer_1_out3, demultiplexer_1_out4,
       demultiplexer_1_out5, random_1_out;

  and and_1 (and_1_out, not_2_out, set);
  not not_1 (not_1_out, set);
  Counter #(.max('h5), .width(3)) counter_1 (
    .count(and_1_out), .Q(counter_1_q), .carry(counter_1_carry), .clk(clock_1_out), .clr(not_1_out));  // open: load, D, up
  Clock clock_1 (.out(clock_1_out));
  Random #(.width(9)) random_1 (.next(not_2_out), .clk(clock_2_out), .out(random_1_out));  // open: clr
  not not_2 (not_2_out, counter_1_carry);
  Clock clock_2 (.out(clock_2_out));
  Demultiplexer #(.select(3), .width(9)) demultiplexer_1 (
    .out1(demultiplexer_1_out1), .out2(demultiplexer_1_out2), .out3(demultiplexer_1_out3),
    .out4(demultiplexer_1_out4), .out5(demultiplexer_1_out5), .in(random_1_out), .sel(counter_1_q));  // open: out0, out6, out7
  Decoder #(.select(3)) decoder_1 (
    .out1(decoder_1_out1), .out2(decoder_1_out2), .out3(decoder_1_out3), .out4(decoder_1_out4),
    .out5(decoder_1_out5), .sel(counter_1_q));  // open: out0, out6, out7, en
  Clock clock_3 (.out(clock_3_out));
  Register #(.width(9)) register_1 (
    .D(demultiplexer_1_out1), .en(decoder_1_out1), .clk(clock_3_out), .Q(out_2));  // open: clr
  Register #(.width(9)) register_2 (
    .D(demultiplexer_1_out2), .en(decoder_1_out2), .clk(clock_3_out), .Q(out_3));  // open: clr
  Register #(.width(9)) register_3 (
    .D(demultiplexer_1_out3), .en(decoder_1_out3), .clk(clock_3_out), .Q(out_4));  // open: clr
  Register #(.width(9)) register_4 (
    .D(demultiplexer_1_out4), .en(decoder_1_out4), .clk(clock_3_out), .Q(out_5));  // open: clr
  Register #(.width(9)) register_5 (
    .D(demultiplexer_1_out5), .en(decoder_1_out5), .clk(clock_3_out), .Q(out_6));  // open: clr
endmodule

// _
module single_display (
  input  [8:0] in_1,
  output [4:0] out_2,
  output [4:0] out_3,
  output [4:0] out_4,
  output [4:0] out_5,
  output [4:0] out_6
);

  wire [4:0] bit_extender_1_out, bit_extender_2_out, bit_extender_3_out;

  assign bit_extender_1_out = {{2{1'b0}}, in_1[2:0]};  // Bit_Extender bit_extender_1
  assign bit_extender_2_out = {{2{1'b0}}, in_1[5:3]};  // Bit_Extender bit_extender_2
  assign bit_extender_3_out = {{2{1'b0}}, in_1[8:6]};  // Bit_Extender bit_extender_3
  Shifter #(.width(5)) shifter_1 (.in(bit_extender_1_out), .\dist (3'b001), .out(out_3));
  Shifter #(.width(5)) shifter_2 (.in(bit_extender_2_out), .\dist (3'b001), .out(out_4));
  Shifter #(.width(5)) shifter_3 (.in(bit_extender_3_out), .\dist (3'b001), .out(out_5));

  assign out_2 = {5{1'b0}};
  assign out_6 = {5{1'b0}};
endmodule

// __
module single_display_mirrored (
  input  [8:0] in_1,
  output [4:0] out_2,
  output [4:0] out_3,
  output [4:0] out_4,
  output [4:0] out_5,
  output [4:0] out_6
);

  wire [4:0] bit_extender_1_out, bit_extender_2_out, bit_extender_3_out;

  assign bit_extender_1_out = {{2{1'b0}}, in_1[2:0]};  // Bit_Extender bit_extender_1
  assign bit_extender_2_out = {{2{1'b0}}, in_1[5:3]};  // Bit_Extender bit_extender_2
  assign bit_extender_3_out = {{2{1'b0}}, in_1[8:6]};  // Bit_Extender bit_extender_3
  Shifter #(.width(5)) shifter_1 (.in(bit_extender_1_out), .\dist (3'b001), .out(out_5));
  Shifter #(.width(5)) shifter_2 (.in(bit_extender_2_out), .\dist (3'b001), .out(out_4));
  Shifter #(.width(5)) shifter_3 (.in(bit_extender_3_out), .\dist (3'b001), .out(out_3));

  assign out_2 = {5{1'b0}};
  assign out_6 = {5{1'b0}};
endmodule
